// Logisim project ula.circ as structural Verilog: 13 circuits, main circuit full-adder
// FA
module full_adder (
  input  A,
  input  B,
  input  Cin,
  output S,
  output Cout
);

  wire and_1_out, and_2_out, or_1_out, xnor_1_out;

  xnor xnor_1 (xnor_1_out, A, B);
  or or_1 (or_1_out, A, B);
  and and_1 (and_1_out, Cin, or_1_out);
  and and_2 (and_2_out, B, A);
  xnor xnor_2 (S, xnor_1_out, Cin);
  or or_2 (Cout, and_1_out, and_2_out);
endmodule

module \xor  (
  input  [3:0] A,
  input  OP,
  input  [3:0] B,
  output [3:0] A_xor_B
);

  wire xor_1_out, xor_2_out, xor_3_out, xor_4_out;

  xor xor_1 (xor_1_out, A[0], B[0]);
  xor xor_2 (xor_2_out, A[1], B[1]);
  xor xor_3 (xor_3_out, A[2], B[2]);
  xor xor_4 (xor_4_out, A[3], B[3]);
  and and_1 (A_xor_B[0], xor_1_out, OP);
  and and_2 (A_xor_B[1], xor_2_out, OP);
  and and_3 (A_xor_B[2], xor_3_out, OP);
  and and_4 (A_xor_B[3], xor_4_out, OP);
endmodule

module has_overflow (
  input  operation,
  input  signal,
  input  overflow,
  output error,
  output signal_2,
  output Overflow_2
);

  and and_1 (error, ~operation, overflow, signal);  // AND_Gate

  assign Overflow_2 = overflow;
  assign signal_2 = signal;
endmodule

module _2_complement (
  input  AUM,
  input  [3:0] B,
  input  OP,
  output [3:0] S
);

  wire full_adder_1_cout, full_adder_2_cout, full_adder_3_cout, xor_1_out, xor_2_out, xor_3_out, xor_4_out;

  xor xor_1 (xor_1_out, OP, B[0]);
  xor xor_2 (xor_2_out, OP, B[1]);
  xor xor_3 (xor_3_out, OP, B[2]);
  xor xor_4 (xor_4_out, OP, B[3]);
  full_adder full_adder_1 (.A(AUM), .B(xor_1_out), .S(S[0]), .Cin(OP), .Cout(full_adder_1_cout));
  full_adder full_adder_2 (.A(AUM), .B(xor_2_out), .S(S[1]), .Cin(full_adder_1_cout), .Cout(full_adder_2_cout));
  full_adder full_adder_3 (.A(AUM), .B(xor_3_out), .S(S[2]), .Cin(full_adder_2_cout), .Cout(full_adder_3_cout));
  full_adder full_adder_4 (.A(AUM), .B(xor_4_out), .S(S[3]), .Cin(full_adder_3_cout));  // open: Cout
endmodule

module adder_plexer (
  input  AUM,
  input  OP,
  input  [3:0] B,
  input  [3:0] S,
  output [3:0] S0
);

  wire and_1_out, and_2_out, and_3_out, and_4_out, and_5_out, and_6_out, and_7_out, and_8_out, and_9_out,
       and_10_out, and_11_out, and_12_out;

  and and_1 (and_1_out, OP, AUM, B[0]);
  and and_2 (and_2_out, OP, AUM, B[1]);
  and and_3 (and_3_out, OP, AUM, B[2]);
  and and_4 (and_4_out, OP, AUM, B[3]);
  and and_5 (and_5_out, ~OP, S[0]);  // AND_Gate
  and and_6 (and_6_out, ~OP, S[1]);  // AND_Gate
  and and_7 (and_7_out, ~OP, S[2]);  // AND_Gate
  and and_8 (and_8_out, ~OP, S[3]);  // AND_Gate
  and and_9 (and_9_out, OP, S[0]);
  and and_10 (and_10_out, OP, S[1]);
  and and_11 (and_11_out, OP, S[2]);
  and and_12 (and_12_out, OP, S[3]);
  or or_1 (S0[0], and_1_out, and_9_out, and_5_out);
  or or_2 (S0[1], and_2_out, and_10_out, and_6_out);
  or or_3 (S0[2], and_3_out, and_11_out, and_7_out);
  or or_4 (S0[3], and_4_out, and_12_out, and_8_out);
endmodule

module bin_to_dec (
  input  Negativo,
  input  BOL,
  input  ERR,
  input  S2,
  input  S1,
  input  S0,
  output _0,
  output _1,
  output _2,
  output _3,
  output _4,
  output _5,
  output _6,
  output _7,
  output ERR_2,
  output minus_1,
  output minus_2,
  output minus_3,
  output minus_4,
  output minus_5,
  output minus_6,
  output minus_7
);

  wire not_1_out, not_2_out, not_3_out, not_4_out, not_5_out, not_6_out, not_7_out, not_8_out, not_9_out,
       not_10_out, not_11_out, not_12_out, not_13_out, not_14_out, not_15_out, not_16_out, not_17_out,
       not_18_out, not_19_out, not_20_out, not_21_out, not_22_out, not_23_out, not_24_out, not_25_out,
       not_26_out, not_27_out, not_28_out, not_29_out, not_30_out, not_31_out, not_32_out, not_33_out,
       not_34_out, not_35_out, not_36_out, not_37_out, not_38_out, not_39_out, not_40_out, not_41_out,
       not_42_out, not_43_out, not_44_out, not_45_out, not_46_out, not_47_out, not_48_out, not_49_out,
       not_50_out, not_51_out, not_52_out, not_53_out, not_54_out, not_55_out, not_56_out, not_57_out,
       not_58_out, not_59_out;

  not not_1 (not_1_out, Negativo);
  not not_2 (not_2_out, S2);
  not not_3 (not_3_out, S1);
  not not_4 (not_4_out, S0);
  and u__0 (_0, not_1_out, not_2_out, not_3_out, not_4_out, not_5_out, not_6_out);
  not not_5 (not_5_out, ERR);
  not not_6 (not_6_out, BOL);
  not not_7 (not_7_out, S2);
  not not_8 (not_8_out, S1);
  not not_9 (not_9_out, ERR);
  and u__1 (_1, not_7_out, not_8_out, S0, not_9_out, not_10_out, not_11_out);
  not not_10 (not_10_out, BOL);
  not not_11 (not_11_out, Negativo);
  not not_12 (not_12_out, S2);
  not not_13 (not_13_out, S0);
  and u__2 (_2, not_12_out, S1, not_13_out, not_14_out, not_15_out, not_16_out);
  not not_14 (not_14_out, ERR);
  not not_15 (not_15_out, BOL);
  not not_16 (not_16_out, Negativo);
  not not_17 (not_17_out, S2);
  and u__3 (_3, not_17_out, S1, S0, not_18_out, not_19_out, not_20_out);
  not not_18 (not_18_out, ERR);
  not not_19 (not_19_out, BOL);
  not not_20 (not_20_out, Negativo);
  not not_21 (not_21_out, S1);
  not not_22 (not_22_out, S0);
  and u__4 (_4, S2, not_21_out, not_22_out, not_23_out, not_24_out, not_25_out);
  not not_23 (not_23_out, ERR);
  not not_24 (not_24_out, BOL);
  not not_25 (not_25_out, Negativo);
  not not_26 (not_26_out, S1);
  not not_27 (not_27_out, ERR);
  and u__5 (_5, S2, not_26_out, S0, not_27_out, not_28_out, not_29_out);
  not not_28 (not_28_out, BOL);
  not not_29 (not_29_out, Negativo);
  not not_30 (not_30_out, S0);
  not not_31 (not_31_out, ERR);
  and u__6 (_6, S2, S1, not_30_out, not_31_out, not_32_out, not_33_out);
  not not_32 (not_32_out, BOL);
  not not_33 (not_33_out, Negativo);
  and u__7 (_7, S2, S1, S0, not_34_out, not_35_out, not_36_out);
  not not_34 (not_34_out, ERR);
  not not_35 (not_35_out, BOL);
  not not_36 (not_36_out, Negativo);
  and _7_2 (minus_1, S2, S1, S0, not_37_out, not_38_out, Negativo);
  not not_37 (not_37_out, ERR);
  not not_38 (not_38_out, BOL);
  not not_39 (not_39_out, S0);
  not not_40 (not_40_out, ERR);
  and _6_2 (minus_2, S2, S1, not_39_out, not_40_out, not_41_out, Negativo);
  not not_41 (not_41_out, BOL);
  not not_42 (not_42_out, S1);
  and _5_2 (minus_3, S2, not_42_out, S0, not_43_out, not_44_out, Negativo);
  not not_43 (not_43_out, ERR);
  not not_44 (not_44_out, BOL);
  not not_45 (not_45_out, S1);
  not not_46 (not_46_out, S0);
  not not_47 (not_47_out, ERR);
  and _4_2 (minus_4, S2, not_45_out, not_46_out, not_47_out, not_48_out, Negativo);
  not not_48 (not_48_out, BOL);
  not not_49 (not_49_out, S2);
  not not_50 (not_50_out, ERR);
  and _3_2 (minus_5, not_49_out, S1, S0, not_50_out, not_51_out, Negativo);
  not not_51 (not_51_out, BOL);
  not not_52 (not_52_out, S2);
  not not_53 (not_53_out, S0);
  and _2_2 (minus_6, not_52_out, S1, not_53_out, not_54_out, not_55_out, Negativo);
  not not_54 (not_54_out, ERR);
  not not_55 (not_55_out, BOL);
  not not_56 (not_56_out, S2);
  not not_57 (not_57_out, S1);
  and _1_2 (minus_7, not_56_out, not_57_out, S0, not_58_out, not_59_out, Negativo);
  not not_58 (not_58_out, ERR);
  not not_59 (not_59_out, BOL);

  assign ERR_2 = ERR;
endmodule

module display (
  input  BOL,
  input  ERR,
  input  S2,
  input  S1,
  input  S0,
  input  Negativo,
  output A,
  output B,
  output C,
  output D,
  output E,
  output F,
  output G
);

  wire bin_to_dec_1__0, bin_to_dec_1__1, bin_to_dec_1__2, bin_to_dec_1__3, bin_to_dec_1__4, bin_to_dec_1__5,
       bin_to_dec_1__6, bin_to_dec_1__7, bin_to_dec_1_err_2, bin_to_dec_1_minus_1, bin_to_dec_1_minus_2,
       bin_to_dec_1_minus_3, bin_to_dec_1_minus_4, bin_to_dec_1_minus_5, bin_to_dec_1_minus_6,
       bin_to_dec_1_minus_7, or_1_out, or_2_out, or_3_out, or_4_out, or_5_out, or_6_out, or_7_out;

  bin_to_dec bin_to_dec_1 (
    .Negativo(Negativo), .BOL(BOL), .ERR(ERR), .S2(S2), .S1(S1), .S0(S0), ._0(bin_to_dec_1__0),
    ._1(bin_to_dec_1__1), ._2(bin_to_dec_1__2), ._3(bin_to_dec_1__3), ._4(bin_to_dec_1__4),
    ._5(bin_to_dec_1__5), ._6(bin_to_dec_1__6), ._7(bin_to_dec_1__7), .ERR_2(bin_to_dec_1_err_2),
    .minus_1(bin_to_dec_1_minus_1), .minus_2(bin_to_dec_1_minus_2), .minus_3(bin_to_dec_1_minus_3),
    .minus_4(bin_to_dec_1_minus_4), .minus_5(bin_to_dec_1_minus_5), .minus_6(bin_to_dec_1_minus_6),
    .minus_7(bin_to_dec_1_minus_7));
  or or_1 (or_1_out, bin_to_dec_1__1, bin_to_dec_1_minus_1);
  or or_2 (or_2_out, bin_to_dec_1__2, bin_to_dec_1_minus_2);
  or or_3 (or_3_out, bin_to_dec_1__3, bin_to_dec_1_minus_3);
  or or_4 (or_4_out, bin_to_dec_1__4, bin_to_dec_1_minus_4);
  or or_5 (or_5_out, bin_to_dec_1__5, bin_to_dec_1_minus_5);
  or or_6 (or_6_out, bin_to_dec_1__6, bin_to_dec_1_minus_6);
  or or_7 (or_7_out, bin_to_dec_1__7, bin_to_dec_1_minus_7);
  or or_8 (A, bin_to_dec_1__0, or_2_out, or_3_out, or_5_out, or_6_out, or_7_out, bin_to_dec_1_err_2);
  or or_9 (B, bin_to_dec_1__0, or_1_out, or_2_out, or_3_out, or_4_out, or_7_out);
  or or_10 (C, bin_to_dec_1__0, or_1_out, or_3_out, or_4_out, or_5_out, or_6_out, or_7_out);
  or or_11 (D, bin_to_dec_1__0, or_2_out, or_3_out, or_5_out, or_6_out, bin_to_dec_1_err_2);
  or or_12 (E, bin_to_dec_1__0, or_2_out, or_6_out, bin_to_dec_1_err_2);
  or or_13 (F, bin_to_dec_1__0, or_4_out, or_5_out, or_6_out, bin_to_dec_1_err_2);
  or or_14 (G, or_2_out, or_3_out, or_4_out, or_5_out, or_6_out, bin_to_dec_1_err_2);
endmodule

module display_signals (
  input  A___B,
  input  A___B_2,
  input  A___B_3,
  input  BOOL,
  input  Si,
  input  ERR,
  output A,
  output B,
  output C,
  output D,
  output E,
  output F,
  output Negativo
);

  wire _0_out, _1_out, and_1_out, and_2_out, Negat_out, or_1_out;

  or or_1 (or_1_out, A___B, A___B_2, A___B_3);
  and and_1 (and_1_out, or_1_out, BOOL);
  and and_2 (and_2_out, ~or_1_out, BOOL);  // AND_Gate
  and _0 (_0_out, ~Si, ~ERR, ~and_1_out, and_2_out, ~ERR);  // AND_Gate
  and _1 (_1_out, and_1_out, ~and_2_out, ~ERR, ~Si, ~ERR);  // AND_Gate
  and Negat (Negat_out, Si, ~ERR);  // AND_Gate
  buf or_2 (A, _0_out);  // OR_Gate
  or or_3 (B, _0_out, _1_out);
  or or_4 (C, _0_out, _1_out);
  buf or_5 (D, _0_out);  // OR_Gate
  buf or_6 (E, _0_out);  // OR_Gate
  buf or_7 (F, _0_out);  // OR_Gate
  buf or_8 (Negativo, Negat_out);  // OR_Gate
endmodule

module sum_sub (
  input  [3:0] A,
  input  [3:0] B,
  input  OP,
  input  AUM,
  output OverFlow,
  output A___B,
  output A___B_2,
  output A___B_3,
  output S0,
  output S1,
  output S2,
  output Sinal
);

  wire full_adder_2_cout, full_adder_3_cout, full_adder_4_cout, not_1_out, not_2_out, not_3_out, not_4_out,
       not_5_out, not_6_out, not_7_out, not_8_out, xor_1_out, xor_2_out, xor_3_out, xor_4_out;
  wire [3:0] full_adder_4_s, n2_complement_1_s;

  xor xor_1 (xor_1_out, B[3], OP);
  full_adder full_adder_1 (.A(A[3]), .B(xor_1_out), .S(full_adder_4_s[3]), .Cin(full_adder_2_cout), .Cout(OverFlow));
  xor xor_2 (xor_2_out, B[2], OP);
  full_adder full_adder_2 (
    .A(A[2]), .B(xor_2_out), .S(full_adder_4_s[2]), .Cin(full_adder_3_cout), .Cout(full_adder_2_cout));
  xor xor_3 (xor_3_out, B[1], OP);
  full_adder full_adder_3 (
    .A(A[1]), .B(xor_3_out), .S(full_adder_4_s[1]), .Cin(full_adder_4_cout), .Cout(full_adder_3_cout));
  xor xor_4 (xor_4_out, B[0], OP);
  full_adder full_adder_4 (.A(A[0]), .B(xor_4_out), .S(full_adder_4_s[0]), .Cin(OP), .Cout(full_adder_4_cout));
  adder_plexer adder_plexer_1 (.B(n2_complement_1_s), .S(full_adder_4_s), .AUM(AUM), .OP(OP), .S0({Sinal, S2, S1, S0}));
  not not_1 (not_1_out, full_adder_4_s[0]);
  not not_2 (not_2_out, full_adder_4_s[1]);
  and and_1 (A___B, OP, not_1_out, not_2_out, not_3_out, not_4_out);
  not not_3 (not_3_out, full_adder_4_s[2]);
  not not_4 (not_4_out, full_adder_4_s[3]);
  _2_complement u_2_complement_1 (.B(B), .S(n2_complement_1_s), .AUM(not_8_out), .OP(OP));
  not not_5 (not_5_out, A___B);
  not not_6 (not_6_out, A___B);
  not not_7 (not_7_out, full_adder_4_s[3]);
  and and_2 (A___B_2, OP, not_5_out, full_adder_4_s[3]);
  and and_3 (A___B_3, OP, not_6_out, not_7_out);
  not not_8 (not_8_out, AUM);
endmodule

module selector (
  input  S0,
  input  S1,
  input  S2,
  output Somar,
  output Subtrair,
  output Complemento,
  output AUM,
  output A___B,
  output A___B_2,
  output A___B_3,
  output AND,
  output XOR,
  output OP
);

  and and_1 (Somar, ~S0, ~S1, ~S2);  // AND_Gate
  and and_2 (Subtrair, S0, ~S1, ~S2);  // AND_Gate
  and and_3 (AUM, ~S0, S1, ~S2);  // AND_Gate
  and and_4 (A___B, S0, S1, ~S2);  // AND_Gate
  and and_5 (A___B_2, ~S0, ~S1, S2);  // AND_Gate
  and and_6 (A___B_3, S0, ~S1, S2);  // AND_Gate
  and and_7 (AND, ~S0, S1, S2);  // AND_Gate
  and and_8 (XOR, S0, S1, S2);
  or or_1 (OP, Subtrair, AUM, A___B, XOR, A___B_2, A___B_3, AND);

  assign Complemento = AUM;
endmodule

module \and  (
  input  [3:0] A,
  input  OP,
  input  [3:0] B,
  output [3:0] AandB
);

  wire and_1_out, and_2_out, and_3_out, and_4_out;

  and and_1 (and_1_out, A[0], B[0]);
  and and_2 (and_2_out, A[1], B[1]);
  and and_3 (and_3_out, A[2], B[2]);
  and and_4 (and_4_out, A[3], B[3]);
  and and_5 (AandB[0], and_1_out, OP);
  and and_6 (AandB[1], and_2_out, OP);
  and and_7 (AandB[2], and_3_out, OP);
  and and_8 (AandB[3], and_4_out, OP);
endmodule

module alu_plexer (
  input  Si,
  input  S2,
  input  S1,
  input  S0,
  input  [3:0] A_and_B,
  input  [3:0] A_xor_B,
  input  _110,
  input  _111,
  input  _000,
  input  _001,
  input  _010,
  input  ERR,
  input  A___B,
  input  A___B_2,
  input  A___B_3,
  input  _011,
  input  _100,
  input  _101,
  output A,
  output B,
  output C,
  output D,
  output E,
  output F,
  output S_A,
  output G,
  output S_B,
  output S_C,
  output S_D,
  output S_E,
  output S_F,
  output Negativo
);

  wire and_1_out, and_2_out, and_3_out, and_4_out, and_5_out, and_6_out, and_7_out, and_8_out, and_9_out,
       and_10_out, and_11_out, and_12_out, and_13_out, and_14_out, and_15_out, and_16_out, and_17_out,
       and_18_out, and_19_out, or_1_out, or_2_out, or_3_out, or_4_out, or_5_out, or_6_out, or_7_out,
       or_8_out, or_9_out, or_10_out;

  and and_1 (and_1_out, ~_101, ~_100, _011);  // AND_Gate
  and and_2 (and_2_out, ~_101, _100, ~_011);  // AND_Gate
  and and_3 (and_3_out, _101, ~_100, ~_011);  // AND_Gate
  and and_4 (and_4_out, A___B, and_1_out);
  and and_5 (and_5_out, A___B_2, and_2_out);
  and and_6 (and_6_out, A___B_3, and_3_out);
  or or_1 (or_1_out, _011, _100, _101);
  or or_2 (or_2_out, _000, _001, _010);
  and and_7 (and_7_out, ~_000, ~_010, _001, or_6_out);  // AND_Gate
  and and_8 (and_8_out, Si, or_2_out);
  or or_3 (or_3_out, and_10_out, and_13_out);
  or or_4 (or_4_out, and_8_out, and_12_out);
  or or_5 (or_5_out, or_3_out, and_17_out);
  or or_6 (or_6_out, or_4_out, and_16_out);
  display_signals display_signals_1 (
    .A___B(and_4_out), .A___B_2(and_6_out), .A___B_3(and_5_out), .Si(and_7_out), .ERR(ERR), .BOOL(or_1_out),
    .A(S_A), .B(S_B), .C(S_C), .D(S_D), .E(S_E), .F(S_F), .Negativo(Negativo));
  and and_9 (and_9_out, S0, or_2_out);
  and and_10 (and_10_out, S2, or_2_out);
  and and_11 (and_11_out, S1, or_2_out);
  or or_7 (or_7_out, and_11_out, and_14_out);
  or or_8 (or_8_out, and_9_out, and_15_out);
  or or_9 (or_9_out, or_7_out, and_19_out);
  or or_10 (or_10_out, or_8_out, and_18_out);
  display display_1 (
    .Negativo(ERR), .BOL(and_7_out), .ERR(or_1_out), .S2(or_5_out), .S1(or_9_out), .S0(or_10_out), .A(A),
    .B(B), .C(C), .D(D), .E(E), .F(F), .G(G));
  and and_12 (and_12_out, _110, A_and_B[3]);
  and and_13 (and_13_out, _110, A_and_B[2]);
  and and_14 (and_14_out, _110, A_and_B[1]);
  and and_15 (and_15_out, _110, A_and_B[0]);
  and and_16 (and_16_out, _111, A_xor_B[3]);
  and and_17 (and_17_out, _111, A_xor_B[2]);
  and and_18 (and_18_out, _111, A_xor_B[0]);
  and and_19 (and_19_out, _111, A_xor_B[1]);
endmodule

module main (
  input  A3,
  input  A2,
  input  A1,
  input  A0,
  input  S2,
  input  S1,
  input  S0,
  input  A3_2,
  input  A2_2,
  input  A1_2,
  input  A0_2,
  output Overflow,
  output Signal
);

  wire alu_plexer_1_a, alu_plexer_1_b, alu_plexer_1_c, alu_plexer_1_d, alu_plexer_1_e, alu_plexer_1_f,
       alu_plexer_1_g, alu_plexer_1_negativo, alu_plexer_1_s_a, alu_plexer_1_s_b, alu_plexer_1_s_c,
       alu_plexer_1_s_d, alu_plexer_1_s_e, alu_plexer_1_s_f, has_overflow_1_error, selector_1_a___b,
       selector_1_a___b_2, selector_1_a___b_3, selector_1_and, selector_1_aum, selector_1_complemento,
       selector_1_op, selector_1_somar, selector_1_subtrair, selector_1_xor, sum_sub_1_a___b,
       sum_sub_1_a___b_2, sum_sub_1_a___b_3, sum_sub_1_overflow, sum_sub_1_s0, sum_sub_1_s1, sum_sub_1_s2,
       sum_sub_1_sinal;
  wire [3:0] and_1_aandb, xor_1_a_xor_b;

  selector selector_1 (
    .S0(S0), .S1(S1), .S2(S2), .Somar(selector_1_somar), .Subtrair(selector_1_subtrair),
    .Complemento(selector_1_complemento), .AUM(selector_1_aum), .A___B(selector_1_a___b),
    .A___B_2(selector_1_a___b_2), .A___B_3(selector_1_a___b_3), .AND(selector_1_and), .XOR(selector_1_xor),
    .OP(selector_1_op));
  sum_sub sum_sub_1 (
    .OverFlow(sum_sub_1_overflow), .AUM(selector_1_aum), .A___B(sum_sub_1_a___b),
    .A___B_2(sum_sub_1_a___b_2), .A___B_3(sum_sub_1_a___b_3), .S0(sum_sub_1_s0), .S1(sum_sub_1_s1),
    .S2(sum_sub_1_s2), .Sinal(sum_sub_1_sinal), .A({A3, A2, A1, A0}), .B({A3_2, A2_2, A1_2, A0_2}),
    .OP(selector_1_op));
  has_overflow has_overflow_1 (
    .operation(sum_sub_1_overflow), .signal(sum_sub_1_sinal), .overflow(selector_1_aum),
    .error(has_overflow_1_error), .signal_2(Overflow), .Overflow_2(Signal));
  \xor  xor_1 (.A({A3, A2, A1, A0}), .B({A3_2, A2_2, A1_2, A0_2}), .OP(selector_1_op), .A_xor_B(xor_1_a_xor_b));
  alu_plexer alu_plexer_1 (
    ._000(selector_1_somar), ._001(selector_1_subtrair), ._010(selector_1_complemento),
    .A___B(sum_sub_1_a___b), .A___B_2(sum_sub_1_a___b_3), .A___B_3(sum_sub_1_a___b_2),
    ._011(selector_1_a___b), ._100(selector_1_a___b_2), ._101(selector_1_a___b_3), ._110(selector_1_and),
    ._111(selector_1_xor), .A(alu_plexer_1_a), .B(alu_plexer_1_b), .C(alu_plexer_1_c), .D(alu_plexer_1_d),
    .E(alu_plexer_1_e), .F(alu_plexer_1_f), .S_A(alu_plexer_1_s_a), .G(alu_plexer_1_g),
    .S_B(alu_plexer_1_s_b), .S_C(alu_plexer_1_s_c), .S_D(alu_plexer_1_s_d), .S_E(alu_plexer_1_s_e),
    .S_F(alu_plexer_1_s_f), .Negativo(alu_plexer_1_negativo), .ERR(has_overflow_1_error), .Si(Overflow),
    .S2(sum_sub_1_s2), .S1(sum_sub_1_s1), .S0(sum_sub_1_s0), .A_xor_B(xor_1_a_xor_b), .A_and_B(and_1_aandb));
  \and  and_1 (.A({A3, A2, A1, A0}), .B({A3_2, A2_2, A1_2, A0_2}), .OP(selector_1_op), .AandB(and_1_aandb));
  _7_Segment_Display u_7_segment_display_1 (
    .g(alu_plexer_1_negativo), .f(alu_plexer_1_s_f), .a(alu_plexer_1_s_a), .b(alu_plexer_1_s_b),
    .e(alu_plexer_1_s_e), .d(alu_plexer_1_s_d), .c(alu_plexer_1_s_c));  // open: dp
  _7_Segment_Display u_7_segment_display_2 (
    .g(alu_plexer_1_g), .f(alu_plexer_1_f), .a(alu_plexer_1_a), .b(alu_plexer_1_b), .e(alu_plexer_1_e),
    .d(alu_plexer_1_d), .c(alu_plexer_1_c));  // open: dp
endmodule
